// Logisim project cpu.circ as structural Verilog: 3 circuits, main circuit main
module main (
  input  [31:0] INSTRUCTION,
  input  CLOCK,
  output [31:0] FETCH_ADDRESS,
  output [31:0] ra,
  output [31:0] sp,
  output [31:0] t0,
  output [31:0] t1,
  output [31:0] t2,
  output [31:0] s0,
  output [31:0] s1,
  output [31:0] a0
);

  wire Asel, BrEq, BrLt, BrUn, Bsel, MemRW, PCsel, RegWEn;
  wire [1:0] WBsel;
  wire [2:0] IMMsel;
  wire [3:0] ALUsel;
  wire [31:0] ALUresult, DataA, DataB, Imm, MemData, multiplexer_1_out, multiplexer_2_out, multiplexer_3_out,
       PC_4;

  Adder #(.width(32)) adder_1 (.a(FETCH_ADDRESS), .b(32'h1), .out(PC_4));  // open: cin, cout
  Register #(.width(32)) PC (.D(PC_4), .clk(CLOCK), .Q(FETCH_ADDRESS));  // open: en, clr
  controller controller_1 (
    .BrUn(BrUn), .IMMsel(IMMsel), .BrLt(BrLt), .INSTRUCTION(INSTRUCTION), .WBsel(WBsel), .BrEq(BrEq),
    .ALUsel(ALUsel), .PCsel(PCsel), .MemRW(MemRW), .RegWEn(RegWEn), .Asel(Asel), .Bsel(Bsel));
  Multiplexer #(.select(2), .width(32), .enable("false")) multiplexer_1 (
    .in0(MemData), .in1(ALUresult), .in2(PC_4), .out(multiplexer_1_out), .sel(WBsel));  // open: in3
  Multiplexer #(.width(32), .enable("false")) multiplexer_2 (
    .in0(DataA), .in1(FETCH_ADDRESS), .out(multiplexer_2_out), .sel(Asel));
  Multiplexer #(.width(32), .enable("false")) multiplexer_3 (
    .in0(DataB), .in1(Imm), .out(multiplexer_3_out), .sel(Bsel));
  alu Arithmetic_Logic_Unit (.A(multiplexer_2_out), .B(multiplexer_3_out), .ALUSel(ALUsel), .Result(ALUresult));
  regfile_main RegFile (
    .rs2(INSTRUCTION[24:20]), .rd(INSTRUCTION[11:7]), .Read_Data_1(DataA), .Read_Data_2(DataB), .ra(ra),
    .sp(sp), .t0(t0), .t1(t1), .t2(t2), .s0(s0), .s1(s1), .a0(a0), .rs1(INSTRUCTION[19:15]),
    .Write_Data(multiplexer_1_out), .RegWEn(RegWEn), .clk(CLOCK));  // open: out_17
  mem_main DMEM (.WriteAddr(ALUresult), .WriteData(DataB), .MemRW(MemRW), .ReadData(MemData), .clk(CLOCK));
  Branch_comp branch_comp_1 (.BrLt(BrLt), .BrEq(BrEq), .BrUn(BrUn), .DataB(DataB), .DataA(DataA));

  // Other names for the same wires on the sheet: clk = CLOCK; fetch_addr[31:0] = FETCH_ADDRESS;
  //   PC[31:0] = FETCH_ADDRESS; Rd[4:0] = INSTRUCTION[11:7]; Rs1[4:0] = INSTRUCTION[19:15];
  //   Rs2[4:0] = INSTRUCTION[24:20]

  // Notes on the sheet:
  //   Output
  //   Inputs/Outputs from run.circ. DO NOT MOVE THESE.
  //   Inputs
  //   Inputs/Outputs from run.circ. DO NOT MOVE THESE.
endmodule

module controller (
  input  [31:0] INSTRUCTION,
  input  BrEq,
  input  BrLt,
  output [3:0] ALUsel,
  output [2:0] IMMsel,
  output PCsel,
  output BrUn,
  output MemRW,
  output Asel,
  output Bsel,
  output [1:0] WBsel,
  output RegWEn
);

  wire and_2_out, and_3_out, and_4_out, and_5_out, comparator_1_gt, comparator_11_eq, comparator_12_eq,
       comparator_13_eq, comparator_14_eq, comparator_15_eq, I, IJ, IL, nor_1_out, or_2_out, or_3_out,
       or_5_out, or_6_out, or_7_out, or_8_out, R, SB, UA, UJ, UL, xnor_1_out;
  wire [3:0] bit_extender_1_out, bit_extender_2_out, bit_extender_3_out, controlled_buffer_1_out,
       controlled_buffer_2_out, controlled_buffer_3_out;

  not not_1 (Bsel, R);
  Comparator #(.width(3)) comparator_1 (.a(INSTRUCTION[14:12]), .b(3'b101), .gt(comparator_1_gt));  // open: eq, lt
  and and_1 (BrUn, comparator_1_gt, SB);
  Comparator #(.width(5), .mode("unsigned")) comparator_2 (.a(INSTRUCTION[6:2]), .b(5'b01100), .eq(R));  // open: gt, lt
  Comparator #(.width(5), .mode("unsigned")) comparator_3 (
    .a(INSTRUCTION[6:2]), .b({5{1'b0}}), .eq(IL));  // open: gt, lt
  Comparator #(.width(5), .mode("unsigned")) comparator_4 (.a(INSTRUCTION[6:2]), .b(5'b00100), .eq(I));  // open: gt, lt
  Comparator #(.width(5), .mode("unsigned")) comparator_5 (
    .a(INSTRUCTION[6:2]), .b(5'b01000), .eq(MemRW));  // open: gt, lt
  Comparator #(.width(5), .mode("unsigned")) comparator_6 (
    .a(INSTRUCTION[6:2]), .b(5'b11000), .eq(SB));  // open: gt, lt
  Comparator #(.width(5), .mode("unsigned")) comparator_7 (
    .a(INSTRUCTION[6:2]), .b(5'b00101), .eq(UA));  // open: gt, lt
  Comparator #(.width(5), .mode("unsigned")) comparator_8 (
    .a(INSTRUCTION[6:2]), .b(5'b01101), .eq(UL));  // open: gt, lt
  Comparator #(.width(5), .mode("unsigned")) comparator_9 (
    .a(INSTRUCTION[6:2]), .b(5'b11011), .eq(UJ));  // open: gt, lt
  Comparator #(.width(5), .mode("unsigned")) comparator_10 (
    .a(INSTRUCTION[6:2]), .b(5'b11001), .eq(IJ));  // open: gt, lt
  or or_1 (Asel, UA, SB, UJ);
  assign bit_extender_1_out = {{1{1'b1}}, INSTRUCTION[14:12]};  // Bit_Extender bit_extender_1
  assign controlled_buffer_1_out = INSTRUCTION[28] ? bit_extender_1_out : 4'bz;  // Controlled_Buffer controlled_buffer_1
  assign controlled_buffer_2_out = xnor_1_out ? bit_extender_2_out : 4'bz;  // Controlled_Buffer controlled_buffer_2
  assign bit_extender_2_out = {{1{1'b0}}, INSTRUCTION[14:12]};  // Bit_Extender bit_extender_2
  xnor xnor_1 (xnor_1_out, INSTRUCTION[30], INSTRUCTION[28]);
  assign controlled_buffer_3_out = INSTRUCTION[30] ? 4'b0011 : 4'bz;  // Controlled_Buffer controlled_buffer_3
  or or_2 (or_2_out, IL, I, IJ);
  or or_3 (or_3_out, UA, UL);
  or or_4 (RegWEn, R, UJ, UA, IJ, UL, I);
  assign ALUsel = R ? controlled_buffer_1_out : 4'bz;  // Controlled_Buffer controlled_buffer_4
  assign ALUsel = R ? controlled_buffer_2_out : 4'bz;  // Controlled_Buffer controlled_buffer_5
  assign ALUsel = R ? controlled_buffer_3_out : 4'bz;  // Controlled_Buffer controlled_buffer_6
  Priority_Encoder priority_encoder_1 (
    .in0(R), .in1(or_2_out), .in2(or_3_out), .in3(MemRW), .in4(SB), .in5(UJ), .out(IMMsel));  // open: in6, in7, en_in, gs, en_out
  nor nor_1 (nor_1_out, IL, IJ, UJ);
  or or_5 (or_5_out, IJ, UJ);
  assign ALUsel = UL ? 4'b0001 : 4'bz;  // Controlled_Buffer controlled_buffer_7
  assign bit_extender_3_out = {{1{1'b0}}, INSTRUCTION[14:12]};  // Bit_Extender bit_extender_3
  assign ALUsel = or_6_out ? 4'b0000 : 4'bz;  // Controlled_Buffer controlled_buffer_8
  or or_6 (or_6_out, SB, UJ, IL, IJ, UA);
  assign ALUsel = I ? bit_extender_3_out : 4'bz;  // Controlled_Buffer controlled_buffer_9
  Priority_Encoder #(.select(2)) priority_encoder_2 (
    .in0(nor_1_out), .in1(IL), .in2(or_5_out), .out(WBsel));  // open: in3, gs, en_out, en_in
  Comparator #(.width(3), .mode("unsigned")) comparator_11 (
    .a(INSTRUCTION[14:12]), .b(3'b100), .eq(comparator_11_eq));  // open: gt, lt
  or or_7 (or_7_out, comparator_11_eq, comparator_12_eq);
  Comparator #(.width(3), .mode("unsigned")) comparator_12 (
    .a(INSTRUCTION[14:12]), .b(3'b110), .eq(comparator_12_eq));  // open: gt, lt
  Comparator #(.width(3), .mode("unsigned")) comparator_13 (
    .a(INSTRUCTION[14:12]), .b(3'b000), .eq(comparator_13_eq));  // open: gt, lt
  Comparator #(.width(3), .mode("unsigned")) comparator_14 (
    .a(INSTRUCTION[14:12]), .b(3'b001), .eq(comparator_14_eq));  // open: gt, lt
  Comparator #(.width(3), .mode("unsigned")) comparator_15 (
    .a(INSTRUCTION[14:12]), .b(3'b111), .eq(comparator_15_eq));  // open: gt, lt
  and and_2 (and_2_out, or_7_out, BrLt);
  and and_3 (and_3_out, comparator_13_eq, BrEq);
  and and_4 (and_4_out, comparator_14_eq, ~BrEq);  // AND_Gate
  and and_5 (and_5_out, comparator_15_eq, ~BrEq, ~BrLt);  // AND_Gate
  or or_8 (or_8_out, and_2_out, and_3_out, and_4_out, and_5_out);
  and and_6 (PCsel, or_8_out, SB);

  // Other names for the same wires on the sheet: opcode[4:0] = INSTRUCTION[6:2]; func3[2:0] = INSTRUCTION[14:12];
  //   Ins28 = INSTRUCTION[28]; Ins30 = INSTRUCTION[30]; S = MemRW

  // Notes on the sheet:
  //   Bsel
  //   BrUn
  //   and_1 drives only 0 and floats otherwise
  //   MenRW
  //   Asel
  //   R
  //   ALUsel
  //   U_type
  //   I_type
  //   RegWEn
  //   IMMsel
  //   UL
  //   I
  //   SB_UJ_IJ_UA_IL
  //   WBsel
  //   and_2 drives only 0 and floats otherwise
  //   and_3 drives only 0 and floats otherwise
  //   and_4 drives only 0 and floats otherwise
  //   and_5 drives only 0 and floats otherwise
  //   PCsel
  //   and_6 drives only 0 and floats otherwise
endmodule

module Branch_comp (
  input  [31:0] DataA,
  input  [31:0] DataB,
  input  BrUn,
  output BrEq,
  output BrLt
);

  wire comparator_2_lt, comparator_3_lt;

  Comparator #(.width(32)) comparator_1 (.a(DataA), .b(DataB), .eq(BrEq));  // open: gt, lt
  Comparator #(.width(32)) comparator_2 (.a(DataA), .b(DataB), .lt(comparator_2_lt));  // open: gt, eq
  Comparator #(.width(32), .mode("unsigned")) comparator_3 (
    .a(DataA), .b(DataB), .lt(comparator_3_lt));  // open: gt, eq
  Multiplexer #(.enable("false")) multiplexer_1 (.in0(comparator_2_lt), .in1(comparator_3_lt), .out(BrLt), .sel(BrUn));
endmodule
